# Fritzing sketch CircuitoMotorGaraje (saved by Fritzing 0.9.3b)
breadboards: 2

parts:
  U1 = G3VM-61E1 [package=g3vm-61e1]
  U2 = G3VM-61E1 [package=g3vm-61e1]
  S1 = Toggle Switch [package=THT]
  S2 = Pushbutton [package="[THT]"]
  U3 = atmega328 [package=dip]
  XTAL1 = Crystal [frequency="16 Mhz" package=THT]
  C1 = Ceramic Capacitor [capacitance=22pF package="100 mil [THT, multilayer]"]
  C2 = Ceramic Capacitor [capacitance=22pF voltage=6.3V package="100 mil [THT, multilayer]"]
  R2 = Resistor [tolerance=±5% resistance=10k package=THT]
  R1 = Resistor [tolerance=±5% resistance=10k package=THT]
  J1 = Screw terminal - 2 pins [package=THT]  # not connected
  LED1 = LED - 5mm [color="Red (633nm)" package="5 mm [THT]"]
  R3 = Resistor [tolerance=±5% resistance=470 package=THT]
  R4 = Resistor [tolerance=±5% resistance=10k package=THT]
  R5 = Resistor [tolerance=±5% resistance=10k package=THT]
  D1 = Rectifier Diode [part_number=1N4001 package="300 mil [THT]"]
  D2 = Rectifier Diode [part_number=1N4001 package="300 mil [THT]"]
  U4 = Voltage Regulator - 5V [package="TO220 [THT]"]  # not connected

nets:
  N1: U1.P$1, U2.P$1, S1.COM, S2.Pin_3, S2.Pin_4, U3.VCC, U3.AVCC, U3.AREF, D1.cathode, D2.cathode
  N2: U1.P$2, U2.P$2, D1.anode, D2.anode
  N3: U1.P$3, U3.D8
  N4: U2.P$3, U3.D7
  N5: S1.L1, U3.D12, R5.Pin_0
  N6: S1.L2, U3.D11_(PWM), R4.Pin_0
  N7: S2.Pin_1, S2.Pin_2, U3.D2, R1.Pin_0
  N8: U3.RESET, R2.Pin_1
  N9: U3.D3_(PWM), R3.Pin_0
  N10: U3.GND, C1.0, C2.1, R2.Pin_0, R1.Pin_1, LED1.cathode, R4.Pin_1, R5.Pin_1
  N11: U3.XLAT1, XTAL1.pin_1, C1.1
  N12: U3.XLAT2, XTAL1.pin_0, C2.0
  N13: LED1.anode, R3.Pin_1

// code stored in the sketch: CircuitoMotorGaraje.ino

/**
  @file CircuitoMotorGaraje.ino
  @brief Controlador del motor de la puerta del garaje
  @author Pablo Rocamora pablojoserocamora@gmail.com
  @date 11/06/2018
*/

#include "CircuitoMotorGaraje.h"

#define MODO_DEBUG true



/**
   Metodo para comprobar si hemos pulsado el boton, retorna true si se ha pulsado y false en caso contrario
   Guarda el estado en el que esta.
*/
bool isClickButton() {
  bool clicked = false;
  int reading = digitalRead(CLICK_BUTTON);
  if (reading == HIGH && millis() - time > debounce) {
    time = millis();
    clicked = true;
  }

  return clicked;
  Serial.println(String(clicked));
}

/**
   Metodo para obtener el pin al que hay que aplicar voltaje para accionar el rele
*/
int getPinRelay() {
  int in = digitalRead(IS_CLOSE_DOOR);
  if (in == HIGH) {
    if (MODO_DEBUG)
      Serial.println("ABRIR");

    return RELAY_OPEN_DOOR;  //7
  }
  if (MODO_DEBUG)
    Serial.println("CERRAR");

  return RELAY_CLOSE_DOOR; //8
}

bool finCarrera(int relay) {
  int pin;
  if (relay == RELAY_OPEN_DOOR)
    pin = IS_OPEN_DOOR;
  else
    pin = IS_CLOSE_DOOR;

  int in = digitalRead(pin);

  if (MODO_DEBUG) {
    Serial.println(String(RELAY_OPEN_DOOR) + ": " + String(digitalRead(RELAY_OPEN_DOOR)));
    Serial.println(String(RELAY_CLOSE_DOOR) + ": " + String(digitalRead(RELAY_CLOSE_DOOR)));
    Serial.println(String(IS_CLOSE_DOOR) + ": " + String(digitalRead(IS_CLOSE_DOOR)));
    Serial.println(String(IS_OPEN_DOOR) + ": " + String(digitalRead(IS_OPEN_DOOR)));
    Serial.println(String(in == HIGH));
    Serial.println();
  }
  if (in == HIGH)
    return true;
  return false;
}


void pause(int pin) {
  digitalWrite(pin, LOW);
}

void play() {
  long inicio = millis();
  long fin = inicio + 10000; //tiempo maximo funcionando

  int relay =  getPinRelay();
  digitalWrite(relay, HIGH);
  Serial.println( "pin: " + String(relay));

  while (!finCarrera(relay)/* || millis() < fin*/) {
    Serial.println("play");

    if (isClickButton())
      pause(relay);
    delay(1000);
  }
  Serial.println("Termina play");
  digitalWrite(relay, LOW);
}



void setup() {
  if (MODO_DEBUG) {
    Serial.begin(115200);
    Serial.println("Inicio");
  }

  pinMode(RELAY_OPEN_DOOR, OUTPUT);
  pinMode(RELAY_CLOSE_DOOR, OUTPUT);
  pinMode(IS_OPEN_DOOR, INPUT);
  pinMode(IS_CLOSE_DOOR, INPUT);
  pinMode(CLICK_BUTTON, INPUT);
  pinMode(LED_OK, OUTPUT);

  digitalWrite(LED_OK, HIGH);
}

void loop() {
  if (isClickButton()) {
    play();
  }
  delay(100);
}
